// Logisim project 4_column_Kmaps.circ as structural Verilog: 1 circuit, main circuit main
module main (
  input  A1,
  input  A0,
  input  B1,
  input  B0,
  output S2,
  output S1,
  output S0
);

  wire A0_nB1_out, A0B0_out, A0B0_tilde_out, A1_B1_out, A1B1_out, and_1_out;

  and A0B0 (A0B0_out, A0, B0);
  xor A1_B1 (A1_B1_out, A1, B1);
  and A1B1 (A1B1_out, A1, B1);
  and A0_nB1 (A0_nB1_out, ~A0, B1);  // AND_Gate
  and A0B0_tilde (A0B0_tilde_out, A0, ~B0);  // AND_Gate
  and and_1 (and_1_out, A0B0_out, A1_B1_out);
  or or_1 (S0, A0_nB1_out, A0B0_tilde_out);
  or or_2 (S2, and_1_out, A1B1_out);

  // Notes on the sheet:
  //   INPUTS
endmodule
