// Logisim project TwosComp.circ as structural Verilog: 1 circuit, main circuit main
module main (
  input  A,
  input  B,
  input  C,
  output D,
  output E,
  output F,
  output G
);

  wire A_prime_B_C_out, AB_prime_C_out, B_C_out;

  or A_B_C (D, A, B, C);
  or B_C (B_C_out, B, C);
  xor BxorC (F, B, C);
  and A_prime_B_C (A_prime_B_C_out, ~A, B_C_out);  // AND_Gate
  and AB_prime_C (AB_prime_C_out, C, ~B, A);  // AND_Gate
  or A_prime_B_C__AB_prime_C (E, A_prime_B_C_out, AB_prime_C_out);

  assign G = C;
endmodule
