// Logisim project Wilt_HW4.circ as structural Verilog: 1 circuit, main circuit main
module main (
  input  A,
  input  B,
  input  C,
  input  D,
  output S5,
  output S4,
  output S3,
  output S2,
  output S1,
  output S0
);

  wire S3_2_out, S3_out, S4_2_out, S4_out;

  and u_S5 (S5, C, B, A);
  and u_S4 (S4_out, A, ~B, C);  // AND_Gate
  and S4_2 (S4_2_out, A, ~C);  // AND_Gate
  and u_S3 (S3_out, B, ~C);  // AND_Gate
  and S3_2 (S3_2_out, ~A, B, C);  // AND_Gate
  xor u_S1 (S1, B, C);
  or S4_3 (S4, S4_out, S4_2_out);
  or S3_3 (S3, S3_out, S3_2_out);
  or u_S2 (S2, S4_out, S4_2_out, S3_2_out);

  assign S0 = D;

  // Notes on the sheet:
  //   Input
  //   S5 = ABC
  //   S3 = BC~ + A~BC
  //   S4 = AB~C + AC~
  //   S1 = BxorC
  //   S0 = D
  //   S2 = AB~C + AC~ + A~BC
  //   Output
endmodule
