// Logisim project Wilt_HW5.circ as structural Verilog: 1 circuit, main circuit main
module main (
  input  A3,
  input  A2,
  input  A1,
  input  A0,
  input  B3,
  input  B2,
  input  B1,
  input  B0,
  output Overflow,
  output O3,
  output O2,
  output O1,
  output O0
);

  wire and_1_out, and_2_out, and_3_out, and_4_out, and_5_out, and_6_out, and_7_out, and_8_out, and_9_out,
       and_10_out, and_11_out, and_12_out, and_13_out, and_14_out, and_15_out, and_16_out, or_1_out,
       or_2_out, or_3_out, or_4_out, xor_1_out, xor_2_out, xor_3_out, xor_4_out, xor_5_out, xor_6_out,
       xor_7_out, xor_8_out, xor_9_out, xor_10_out, xor_11_out, xor_12_out, xor_13_out, xor_14_out,
       xor_15_out, xor_16_out;

  or or_1 (or_1_out, B3, A3);
  xor xor_1 (xor_1_out, B3, B0);
  xor xor_2 (xor_2_out, A3, A0);
  xor xor_3 (xor_3_out, B3, B1);
  xor xor_4 (xor_4_out, A3, A1);
  xor xor_5 (xor_5_out, B3, B2);
  xor xor_6 (xor_6_out, A3, A2);
  xor xor_7 (xor_7_out, B3, B3);
  xor xor_8 (xor_8_out, A3, A3);
  xor xor_9 (xor_9_out, xor_1_out, xor_2_out);
  xor xor_10 (xor_10_out, xor_3_out, xor_4_out);
  xor xor_11 (xor_11_out, xor_5_out, xor_6_out);
  xor xor_12 (xor_12_out, xor_7_out, xor_8_out);
  xor xor_13 (xor_13_out, or_1_out, xor_9_out);
  xor xor_14 (xor_14_out, or_2_out, xor_10_out);
  xor xor_15 (xor_15_out, or_3_out, xor_11_out);
  xor xor_16 (xor_16_out, or_4_out, xor_12_out);
  and and_1 (and_1_out, xor_1_out, xor_2_out);
  or or_2 (or_2_out, and_1_out, and_2_out);
  and and_2 (and_2_out, or_1_out, xor_9_out);
  and and_3 (and_3_out, xor_3_out, xor_4_out);
  or or_3 (or_3_out, and_3_out, and_4_out);
  and and_4 (and_4_out, or_2_out, xor_10_out);
  and and_5 (and_5_out, xor_5_out, xor_6_out);
  or or_4 (or_4_out, and_5_out, and_6_out);
  and and_6 (and_6_out, or_3_out, xor_11_out);
  and and_7 (and_7_out, xor_7_out, xor_8_out);
  or or_5 (Overflow, and_7_out, and_8_out);
  and and_8 (and_8_out, or_4_out, xor_12_out);
  and and_9 (and_9_out, xor_13_out, ~Overflow);  // AND_Gate
  and and_10 (and_10_out, 1'b0, Overflow);
  and and_11 (and_11_out, xor_14_out, ~Overflow);  // AND_Gate
  and and_12 (and_12_out, 1'b0, Overflow);
  and and_13 (and_13_out, xor_15_out, ~Overflow);  // AND_Gate
  and and_14 (and_14_out, 1'b0, Overflow);
  and and_15 (and_15_out, xor_16_out, ~Overflow);  // AND_Gate
  and and_16 (and_16_out, 1'b0, Overflow);
  or or_6 (O0, and_9_out, and_10_out);
  or or_7 (O1, and_11_out, and_12_out);
  or or_8 (O2, and_13_out, and_14_out);
  or or_9 (O3, and_15_out, and_16_out);

  // Notes on the sheet:
  //   Input A
  //   Input B
  //   NEGATIVE?
  //   4 BIT ADDER w/ TWO'S COMPLEMENT
  //   FULL ADDERS
  //   Cin
  //   Cin
  //   Cin
  //   Cin
  //   sum
  //   sum
  //   sum
  //   sum
  //   Cout
  //   Cout
  //   Cout
  //   Cout
  //   OVERFLOW SYSTEM?
  //   Ouput
endmodule
