// Logisim project Wilt_Lab7.circ as structural Verilog: 1 circuit, main circuit main
module main (
  input  A,
  input  B,
  input  C,
  output S5,
  output S4,
  output S3,
  output S2,
  output S1,
  output S0
);

  wire AB_tilde_out, AC_out, AXORB_out;

  and AB (S5, A, B);
  and AB_tilde (AB_tilde_out, A, ~B);  // AND_Gate
  and AC (AC_out, A, C);
  xor AXORB (AXORB_out, A, B);
  and BC_tilde (S2, B, ~C);  // AND_Gate
  or or_1 (S4, AB_tilde_out, AC_out);
  and xorC (S3, AXORB_out, C);

  assign S0 = C;
  assign S1 = 1'b0;

  // Notes on the sheet:
  //   Hardcode
  //   INPUT (unsigned binary)
  //   S5 - A and B
  //   S2 - B and Cnot
  //   S1 - hardcoded to 0
  //   S0 - hardcoded to C
  //   S4 - ABnot + AC
  //   S3 - C(AXORB)
  //   OUTPUT (unsigned binary)
endmodule
